# Fritzing sketch board (saved by Fritzing 0.9.3b)
circuit board: 11.7554cm x 6.59937cm
breadboards: 1

parts:
  S0 = SWITCH-MOMENTARY-2 [package=tactile-pth-12mm]
  S1 = SWITCH-MOMENTARY-2 [package=tactile-pth-12mm]
  S2 = SWITCH-MOMENTARY-2 [package=tactile-pth-12mm]
  S3 = SWITCH-MOMENTARY-2 [package=tactile-pth-12mm]
  S4 = SWITCH-MOMENTARY-2 [package=tactile-pth-12mm]
  S5 = SWITCH-MOMENTARY-2 [package=tactile-pth-12mm]
  S6 = SWITCH-MOMENTARY-2 [package=tactile-pth-12mm]
  S7 = SWITCH-MOMENTARY-2 [package=tactile-pth-12mm]
  IC1 = IC, DIP package, 28 pins [chip_label=ATMega]
  S8 = SWITCH-MOMENTARY-2 [package=tactile-pth-12mm]
  S9 = SWITCH-MOMENTARY-2 [package=tactile-pth-12mm]
  S10 = SWITCH-MOMENTARY-2 [package=tactile-pth-12mm]
  S11 = SWITCH-MOMENTARY-2 [package=tactile-pth-12mm]
  S12 = SWITCH-MOMENTARY-2 [package=tactile-pth-12mm]
  S13 = SWITCH-MOMENTARY-2 [package=tactile-pth-12mm]
  S14 = SWITCH-MOMENTARY-2 [package=tactile-pth-12mm]
  S15 = SWITCH-MOMENTARY-2 [package=tactile-pth-12mm]
  S16 = SWITCH-MOMENTARY-2 [package=tactile-pth-12mm]
  S17 = SWITCH-MOMENTARY-2 [package=tactile-pth-12mm]
  S18 = SWITCH-MOMENTARY-2 [package=tactile-pth-12mm]
  S19 = SWITCH-MOMENTARY-2 [package=tactile-pth-12mm]
  S20 = SWITCH-MOMENTARY-2 [package=tactile-pth-12mm]
  S21 = SWITCH-MOMENTARY-2 [package=tactile-pth-12mm]
  S22 = SWITCH-MOMENTARY-2 [package=tactile-pth-12mm]
  S23 = SWITCH-MOMENTARY-2 [package=tactile-pth-12mm]
  XTAL1 = Crystal [frequency="16 Mhz" package=THT]
  C1 = Ceramic Capacitor [capacitance=100nF package="100 mil [THT, multilayer]"]
  C2 = Ceramic Capacitor [capacitance=1pF package="100 mil [THT, multilayer]"]
  J1 = female pin header, 10 pins [form="♀ (female)"]
  MIDI = female pin header, 3 pins [form="♀ (female)"]
  C3 = Capacitor [package=cap-pth-small-kit]

nets:
  N1: S0.1, IC1.pin15, S8.1, S16.1
  N2: S0.2, S1.2, S2.2, S3.2, S4.2, S5.2, S6.2, S7.2, IC1.pin18
  N3: S1.1, IC1.pin14, S9.1, S17.1
  N4: S2.1, IC1.pin13, S10.1, S18.1
  N5: S3.1, IC1.pin12, S11.1, S19.1
  N6: S4.1, IC1.pin11, S12.1, S20.1
  N7: S5.1, IC1.pin6, S13.1, S21.1
  N8: S6.1, IC1.pin5, S14.1, S22.1
  N9: S7.1, IC1.pin4, S15.1, S23.1
  N10: IC1.pin3, J1.pin10, MIDI.pin3
  N11: IC1.pin7, J1.pin9, MIDI.pin2, C3.1
  N12: IC1.pin8, C1.0, C2.0, J1.pin8, MIDI.pin1, C3.2
  N13: IC1.pin9, XTAL1.pin_0, C2.1
  N14: IC1.pin10, XTAL1.pin_1, C1.1
  N15: IC1.pin16, S16.2, S17.2, S18.2, S19.2, S20.2, S21.2, S22.2, S23.2
  N16: IC1.pin17, S8.2, S9.2, S10.2, S11.2, S12.2, S13.2, S14.2, S15.2
  N17: IC1.pin19, J1.pin7
  N18: IC1.pin23, J1.pin6
  N19: IC1.pin24, J1.pin5
  N20: IC1.pin25, J1.pin4
  N21: IC1.pin26, J1.pin3
  N22: IC1.pin27, J1.pin2
  N23: IC1.pin28, J1.pin1

notes:
  TX
  +V
  GND
  D13
  A0
  A1
  A2
  A3
  A4
  A5
  Chord Keyboard v1.0
  www.clearviewtraining.com
  RST
  RX
  D2
  D3
  D4
  XTAL1
  XTAL2
  D5
  D6
  D7
  D8
  D9
  D10
  D11
  D12
  AVCC
  AREF
  OUT
